# Fritzing sketch CE_Dissertation (saved by Fritzing 1.0.2b)
circuit board: 8.23229cm x 5.13962cm
breadboards: 1

parts:
  A1 = ESP32 wrover cam
  M2 = BME680 Module [part_number=CJMCU-680]
  U1 = LIPO-1000mAh [package=lipo-1000]
  S1 = Toggle Switch [package=THT]
  LED3 = LED - 5mm [color="Red (633nm)" current=0.030A package="5 mm [THT]"]
  R1 = Resistor [tolerance=±5% resistance=220 package="0603 [SMD]"]
  LED4 = LED - 5mm [color="Red (633nm)" current=0.030A package="5 mm [THT]"]
  R2 = Resistor [tolerance=±5% resistance=220 package="0603 [SMD]"]
  S2 = Momentary Switch [package=ksa_sealed_tac_switch]
  A2 = GY-BMP280 Breakout  # not connected

nets:
  N1: A1.Pin_1, M2.VCC, U1.+, S1.L1, S1.COM, S1.L2
  N2: A1.Pin_14, A1.Pin_29, A1.Pin_30, A1.Pin_40, M2.GND, U1.-, LED3.cathode, LED3.anode, R1.Pin_1, LED4.cathode, LED4.anode, R2.Pin_1
  N3: A1.Pin_35, M2.SDA
  N4: A1.Pin_38, M2.SCL
  N5: S2.1, S2.3
  N6: S2.2, S2.4

custom parts:
  ESP32 wrover cam: ESP32-WROVER -> A powerful and small controller with onboard camera and wireless.
  BME680 Module: Bosch BME680 Development Module The BME680 is a digital 4-in-1 sensor that measures air quality [gas], humidity, pressure and temperature. Links: BME680 product datasheet
