# Fritzing sketch CE_Dissertation (saved by Fritzing 1.0.2b)
circuit board: 5.99967cm x 3.08477cm
breadboards: 1

parts:
  A1 = ESP32 wrover cam
  Lipo_Battery = LIPO-1000mAh [package=lipo-1000]
  BME680 = BME680 Module [part_number=CJMCU-680]
  S1 = Toggle Switch [package=THT]
  LED_Resistor = Resistor [tolerance=±5% resistance=220 package="2512 [SMD]"]
  LED_Resistor_2 = Resistor [tolerance=±5% resistance=220 package="2512 [SMD]"]
  Power_Led = LED - 3mm [color="Yellow (592nm)" current=0.030A package="3 mm [THT]"]
  Lipo_Battery_Charger = TP4056 [chip_label=TP4056 package="DIP (Dual Inline) [THT]"]
  WebSocket_Led = LED - 3mm [color="Yellow (592nm)" current=0.030A package="3 mm [THT]"]

nets (from the breadboard view):
  N1: A1.Pin_1, BME680.VCC, Lipo_Battery_Charger.pin3
  N2: A1.Pin_7, BME680.SCL
  N3: A1.Pin_8, BME680.SDA
  N4: A1.Pin_14, A1.Pin_30, A1.Pin_40, BME680.GND, LED_Resistor.Pin_1, LED_Resistor_2.Pin_1, Power_Led.cathode, Power_Led.anode, Lipo_Battery_Charger.pin6, WebSocket_Led.cathode, WebSocket_Led.anode
  N5: Lipo_Battery.+, S1.L2
  N6: Lipo_Battery.-, Lipo_Battery_Charger.pin5
  N7: S1.COM, Lipo_Battery_Charger.pin4

custom parts:
  ESP32 wrover cam: ESP32-WROVER -> A powerful and small controller with onboard camera and wireless.
  BME680 Module: Bosch BME680 Development Module The BME680 is a digital 4-in-1 sensor that measures air quality [gas], humidity, pressure and temperature. Links: BME680 product datasheet
  TP4056: A DIP stand-in part for whatever IC you want. With 6 pins on a 300mil dual inline package (DIP) footprint.
